# Fritzing sketch Block_2_Digital_Die_101 (saved by Fritzing 0.9.3b)
breadboards: 1

parts:
  LED1 = LED - 5mm [color="Red (633nm)" package="5 mm [THT]"]
  LED2 = LED - 5mm [color="Red (633nm)" package="5 mm [THT]"]
  LED3 = LED - 5mm [color="Red (633nm)" package="5 mm [THT]"]
  R3 = Resistor [tolerance=±5% resistance=220 package=THT]
  R1 = Resistor [tolerance=±5% resistance=220 package=THT]
  R2 = Resistor [tolerance=±5% resistance=220 package=THT]
  LED4 = LED - 5mm [color="Red (633nm)" package="5 mm [THT]"]
  LED5 = LED - 5mm [color="Red (633nm)" package="5 mm [THT]"]
  LED6 = LED - 5mm [color="Red (633nm)" package="5 mm [THT]"]
  R6 = Resistor [tolerance=±5% resistance=220 package=THT]
  R5 = Resistor [tolerance=±5% resistance=220 package=THT]
  R4 = Resistor [tolerance=±5% resistance=220 package=THT]
  LED7 = LED - 5mm [color="Red (633nm)" package="5 mm [THT]"]
  LED8 = LED - 5mm [color="Red (633nm)" package="5 mm [THT]"]
  LED9 = LED - 5mm [color="Red (633nm)" package="5 mm [THT]"]
  R9 = Resistor [tolerance=±5% resistance=220 package=THT]
  R8 = Resistor [tolerance=±5% resistance=220 package=THT]
  R7 = Resistor [tolerance=±5% resistance=220 package=THT]
  S1 = Tilt Switch [package=THT]
  R10 = Resistor [tolerance=±5% resistance=10k package=THT]
  Part2 = Arduino 101

nets:
  N1: LED1.cathode, LED2.cathode, LED3.cathode, LED4.cathode, LED5.cathode, LED6.cathode, LED7.cathode, LED8.cathode, LED9.cathode, R10.Pin_0, Part2.GND
  N2: LED1.anode, R1.Pin_1
  N3: LED2.anode, R2.Pin_1
  N4: LED3.anode, R3.Pin_0
  N5: R3.Pin_1, Part2.D8
  N6: R1.Pin_0, Part2.D12/MISO
  N7: R2.Pin_0, Part2.D11_PWM/MOSI
  N8: LED4.anode, R4.Pin_1
  N9: LED5.anode, R5.Pin_1
  N10: LED6.anode, R6.Pin_0
  N11: R6.Pin_1, Part2.D5_PWM
  N12: R5.Pin_0, Part2.D6_PWM
  N13: R4.Pin_0, Part2.D7
  N14: LED7.anode, R7.Pin_1
  N15: LED8.anode, R8.Pin_1
  N16: LED9.anode, R9.Pin_0
  N17: R9.Pin_1, Part2.D2
  N18: R8.Pin_0, Part2.D3_PWM
  N19: R7.Pin_0, Part2.D4
  N20: S1.Pin_1, R10.Pin_1, Part2.D9_PWM
  N21: S1.Pin_2, Part2.ioref

custom parts:
  Arduino 101: A learning and development board that delivers the performance and low-power consumption of the Intel® Curie™ Module with the simplicity of Arduino at an entry-level price. It keeps the same robust form factor and peripheral list of the UNO with the addition of onboard Bluetooth LE capabilities and a 6-axis accelerometer/gyro to help you easily expand your creativity into the connected world.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
