# Fritzing sketch Block_2_Fencing_101 (saved by Fritzing 0.9.3b)
breadboards: 1

parts:
  LED1 = LED - 5mm [color="Yellow (595nm)" package="5 mm [THT]"]
  LED2 = LED - 5mm [color="Red (633nm)" package="5 mm [THT]"]
  LED3 = LED - 5mm [color="Green (555nm)" package="5 mm [THT]"]
  LED4 = LED - 5mm [color="Yellow (595nm)" package="5 mm [THT]"]
  R4 = Resistor [tolerance=±5% resistance=220 package=THT]
  R3 = Resistor [tolerance=±5% resistance=220 package=THT]
  S1 = Tilt Switch [package=THT]
  S2 = Tilt Switch [package=THT]
  R6 = Resistor [tolerance=±5% resistance=10k package=THT]
  R5 = Resistor [tolerance=±5% resistance=10k package=THT]
  R2 = Resistor [tolerance=±5% resistance=220 package=THT]
  R1 = Resistor [tolerance=±5% resistance=220 package=THT]
  Part1 = Arduino 101

nets (from the breadboard view):
  N1: LED1.cathode, LED2.cathode, LED3.cathode, LED4.cathode, R6.Pin_0, R5.Pin_1, Part1.GND
  N2: LED1.anode, R4.Pin_0
  N3: LED2.anode, R3.Pin_0
  N4: LED3.anode, R2.Pin_0
  N5: LED4.anode, R1.Pin_0
  N6: R4.Pin_1, Part1.D5_PWM
  N7: R3.Pin_1, Part1.D4
  N8: S1.Pin_1, R6.Pin_1, Part1.D6_PWM
  N9: S1.Pin_2, S2.Pin_1, Part1.ioref
  N10: S2.Pin_2, R5.Pin_0, Part1.D9_PWM
  N11: R2.Pin_1, Part1.D3_PWM
  N12: R1.Pin_1, Part1.D2

custom parts:
  Arduino 101: A learning and development board that delivers the performance and low-power consumption of the Intel® Curie™ Module with the simplicity of Arduino at an entry-level price. It keeps the same robust form factor and peripheral list of the UNO with the addition of onboard Bluetooth LE capabilities and a 6-axis accelerometer/gyro to help you easily expand your creativity into the connected world.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
