# Fritzing sketch Block_2_Pong_101 (saved by Fritzing 0.9.3b)
breadboards: 1

parts:
  LED1 = LED - 5mm [color="Green (555nm)" package="5 mm [THT]"]
  LED2 = LED - 5mm [color="Green (555nm)" package="5 mm [THT]"]
  LED3 = LED - 5mm [color="Green (555nm)" package="5 mm [THT]"]
  LED4 = LED - 5mm [color="Green (555nm)" package="5 mm [THT]"]
  LED5 = LED - 5mm [color="Green (555nm)" package="5 mm [THT]"]
  R1 = Resistor [tolerance=±5% resistance=220 package=THT]
  R2 = Resistor [tolerance=±5% resistance=220 package=THT]
  R3 = Resistor [tolerance=±5% resistance=220 package=THT]
  R4 = Resistor [tolerance=±5% resistance=220 package=THT]
  S1 = Pushbutton [package="[THT]"]
  S2 = Pushbutton [package="[THT]"]
  R8 = Resistor [tolerance=±5% resistance=10k package=THT]
  R9 = Resistor [tolerance=±5% resistance=10k package=THT]
  R10 = Resistor [tolerance=±5% resistance=220 package=THT]
  Part2 = Arduino 101

nets (from the schematic view):
  N1: LED1.cathode, LED2.cathode, LED3.cathode, LED4.cathode, LED5.cathode, R8.Pin_0, R9.Pin_0, Part2.GND
  N2: LED1.anode, R1.Pin_1
  N3: LED2.anode, R2.Pin_1
  N4: LED3.anode, R10.Pin_1
  N5: LED4.anode, R3.Pin_1
  N6: LED5.anode, R4.Pin_1
  N7: R1.Pin_0, Part2.D2
  N8: R2.Pin_0, Part2.D5_PWM
  N9: R3.Pin_0, Part2.D3_PWM
  N10: R4.Pin_0, Part2.D7
  N11: S1.Pin_1, S1.Pin_2, S2.Pin_1, S2.Pin_2, Part2.ioref
  N12: S1.Pin_3, S1.Pin_4, R8.Pin_1, Part2.D6_PWM
  N13: S2.Pin_3, S2.Pin_4, R9.Pin_1, Part2.D9_PWM
  N14: R10.Pin_0, Part2.D4

custom parts:
  Arduino 101: A learning and development board that delivers the performance and low-power consumption of the Intel® Curie™ Module with the simplicity of Arduino at an entry-level price. It keeps the same robust form factor and peripheral list of the UNO with the addition of onboard Bluetooth LE capabilities and a 6-axis accelerometer/gyro to help you easily expand your creativity into the connected world.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
