# Fritzing sketch Block_2_React_101 (saved by Fritzing 0.9.3b)
breadboards: 1

parts:
  LED1 = LED - 5mm [color="Red (633nm)" package="5 mm [THT]"]
  LED2 = LED - 5mm [color="Red (633nm)" package="5 mm [THT]"]
  LED3 = LED - 5mm [color="Red (633nm)" package="5 mm [THT]"]
  J1 = Piezo Speaker
  R1 = Resistor [tolerance=±5% resistance=1M package=THT]
  R2 = Resistor [tolerance=±5% resistance=1M package=THT]
  R3 = Resistor [tolerance=±5% resistance=1M package=THT]
  R4 = Resistor [tolerance=±5% resistance=220 package=THT]
  R5 = Resistor [tolerance=±5% resistance=220 package=THT]
  R6 = Resistor [tolerance=±5% resistance=220 package=THT]
  Part1 = Arduino 101

nets:
  N1: LED1.cathode, LED2.cathode, LED3.cathode, J1.pin1
  N2: LED1.anode, R4.Pin_1
  N3: LED2.anode, R5.Pin_1
  N4: LED3.anode, R6.Pin_1
  N5: J1.pin2, Part1.D8
  N6: R1.Pin_0, R2.Pin_0, R3.Pin_0, Part1.D2
  N7: R1.Pin_1, Part1.D5_PWM
  Aluminium foil: R2.Pin_1, Part1.D4
  N8: R3.Pin_1, Part1.D3_PWM
  N9: R4.Pin_0, Part1.D11_PWM/MOSI
  N10: R5.Pin_0, Part1.D10_PWM/SS
  N11: R6.Pin_0, Part1.D9_PWM

notes:
  Aluminium foil

custom parts:
  Arduino 101: A learning and development board that delivers the performance and low-power consumption of the Intel® Curie™ Module with the simplicity of Arduino at an entry-level price. It keeps the same robust form factor and peripheral list of the UNO with the addition of onboard Bluetooth LE capabilities and a 6-axis accelerometer/gyro to help you easily expand your creativity into the connected world.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
