# Fritzing sketch Block_4_Line_Follower_101 (saved by Fritzing 0.9.3b)
breadboards: 1

parts:
  R1 = Resistor [tolerance=±5% resistance=220 package=THT]
  R2 = Resistor [tolerance=±5% resistance=220 package=THT]
  R3 = Resistor [tolerance=±5% resistance=220 package=THT]
  R4 = Resistor [tolerance=±5% resistance=47k package=THT]
  R5 = Resistor [tolerance=±5% resistance=47k package=THT]
  R6 = Resistor [tolerance=±5% resistance=47k package=THT]
  VCC1 = Battery block 9V
  VCC2 = 4 x AAA Battery Mount
  J1 = Basic Servo
  J2 = Basic Servo
  S1 = CNY70 [package="[THT]"]
  S2 = CNY70 [package="[THT]"]
  S3 = CNY70 [package="[THT]"]
  Part1 = Arduino 101

nets (from the schematic view):
  N1: R1.Pin_0, R2.Pin_0, R3.Pin_1, S1.Collector, S2.Collector, S3.Collector, Part1.ioref
  N2: R1.Pin_1, S1.Anode
  N3: R2.Pin_1, S2.Anode
  N4: R3.Pin_0, S3.Anode
  GND: R4.Pin_0, R5.Pin_0, R6.Pin_0, VCC1.-, VCC2.-, J1.gnd, J2.gnd, S1.Catode, S2.Catode, S3.Catode, Part1.GND
  N5: R4.Pin_1, S3.Emiter
  N6: R5.Pin_1, S2.Emiter
  N7: R6.Pin_1, S1.Emiter
  N8: VCC1.+, Part1.VIN
  VCC: VCC2.+, J1.vcc, J2.vcc
  N9: J1.pulse, Part1.D6_PWM
  N10: J2.pulse, Part1.D9_PWM

custom parts:
  CNY70: IR compact sensor
  Arduino 101: A learning and development board that delivers the performance and low-power consumption of the Intel® Curie™ Module with the simplicity of Arduino at an entry-level price. It keeps the same robust form factor and peripheral list of the UNO with the addition of onboard Bluetooth LE capabilities and a 6-axis accelerometer/gyro to help you easily expand your creativity into the connected world.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
