# Fritzing sketch Block_4_Tickle_Robot_101 (saved by Fritzing 0.9.3b)
breadboards: 1

parts:
  R1 = Resistor [tolerance=±5% resistance=1M package=THT]
  J1 = Basic Servo
  Part1 = Arduino 101

nets:
  N1: R1.Pin_0, Part1.D2
  Aluminium foil: R1.Pin_1, Part1.D3_PWM
  GND: J1.gnd, Part1.GND
  N2: J1.vcc, Part1.ioref
  N3: J1.pulse, Part1.D9_PWM

notes:
  Aluminium foil

custom parts:
  Arduino 101: A learning and development board that delivers the performance and low-power consumption of the Intel® Curie™ Module with the simplicity of Arduino at an entry-level price. It keeps the same robust form factor and peripheral list of the UNO with the addition of onboard Bluetooth LE capabilities and a 6-axis accelerometer/gyro to help you easily expand your creativity into the connected world.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
