# Fritzing sketch Block_05_Nova_beam_101 (saved by Fritzing 0.9.3b)
breadboards: 1

parts:
  Part4 = Arduino 101
  S4 = Pushbutton [package="[THT]"]
  R4 = Resistor [tolerance=±5% resistance=10k package=THT]
  J1 = Piezo Speaker

nets:
  N1: Part4.D8, J1.pin1
  N2: Part4.D10_PWM/SS, S4.Pin_1, S4.Pin_2, R4.Pin_0
  N3: Part4.GND, R4.Pin_1, J1.pin2
  N4: Part4.ioref, S4.Pin_3, S4.Pin_4

custom parts:
  Arduino 101: A learning and development board that delivers the performance and low-power consumption of the Intel® Curie™ Module with the simplicity of Arduino at an entry-level price. It keeps the same robust form factor and peripheral list of the UNO with the addition of onboard Bluetooth LE capabilities and a 6-axis accelerometer/gyro to help you easily expand your creativity into the connected world.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
