# Fritzing sketch Block_05_Space_rover_101 (saved by Fritzing 0.9.3b)
breadboards: 1

parts:
  VCC1 = Battery block 9V
  VCC2 = 4 x AAA Battery Mount
  J1 = Basic Servo
  J2 = Basic Servo
  Part1 = Arduino 101

nets:
  GND: VCC1.-, VCC2.-, J1.gnd, J2.gnd, Part1.GND
  N1: VCC1.+, Part1.VIN
  VCC: VCC2.+, J1.vcc, J2.vcc
  N2: J1.pulse, Part1.D6_PWM
  N3: J2.pulse, Part1.D9_PWM

custom parts:
  Arduino 101: A learning and development board that delivers the performance and low-power consumption of the Intel® Curie™ Module with the simplicity of Arduino at an entry-level price. It keeps the same robust form factor and peripheral list of the UNO with the addition of onboard Bluetooth LE capabilities and a 6-axis accelerometer/gyro to help you easily expand your creativity into the connected world.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
