# Fritzing sketch Module_3_Binary_LP_Schematic_101 (saved by Fritzing 0.9.3b)
breadboards: 1

parts:
  J1 = Piezo Speaker
  R1 = Resistor [tolerance=±5% resistance=220 package=THT]
  R2 = Resistor [tolerance=±5% resistance=220 package=THT]
  R3 = Resistor [tolerance=±5% resistance=220 package=THT]
  R4 = Resistor [tolerance=±5% resistance=47k package=THT]
  R5 = Resistor [tolerance=±5% resistance=47k package=THT]
  R6 = Resistor [tolerance=±5% resistance=47k package=THT]
  S1 = CNY70 [package="[THT]"]
  S2 = CNY70 [package="[THT]"]
  S3 = CNY70 [package="[THT]"]
  Part1 = Arduino 101

nets:
  N1: J1.pin1, Part1.GND
  N2: J1.pin2, Part1.D8
  N3: R1.Pin_0, S1.Anode
  N4: R1.Pin_1, R2.Pin_1, R3.Pin_1, S3.Collector
  N5: R2.Pin_0, S2.Anode
  N6: R3.Pin_0, S3.Anode
  N7: R4.Pin_0, R5.Pin_0, R6.Pin_0, S1.Catode, S2.Catode, S3.Catode
  N8: R4.Pin_1, S1.Emiter
  N9: R5.Pin_1, S2.Emiter
  N10: R6.Pin_1, S3.Emiter
  N11: S1.Collector, S2.Collector

custom parts:
  CNY70: IR compact sensor
  Arduino 101: A learning and development board that delivers the performance and low-power consumption of the Intel® Curie™ Module with the simplicity of Arduino at an entry-level price. It keeps the same robust form factor and peripheral list of the UNO with the addition of onboard Bluetooth LE capabilities and a 6-axis accelerometer/gyro to help you easily expand your creativity into the connected world.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
