# Fritzing sketch Module_3_Drawdio_101 (saved by Fritzing 0.9.3b)
breadboards: 1

parts:
  R1 = Resistor [tolerance=±5% resistance=1M package=THT]
  J1 = Piezo Speaker
  Part2 = Arduino 101

nets:
  N1: R1.Pin_0, Part2.D2
  Pencil.: R1.Pin_1, Part2.D3_PWM
  N2: J1.pin1, Part2.GND
  N3: J1.pin2, Part2.D8

notes:
  Pencil

custom parts:
  Arduino 101: A learning and development board that delivers the performance and low-power consumption of the Intel® Curie™ Module with the simplicity of Arduino at an entry-level price. It keeps the same robust form factor and peripheral list of the UNO with the addition of onboard Bluetooth LE capabilities and a 6-axis accelerometer/gyro to help you easily expand your creativity into the connected world.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
