# Fritzing sketch Module_3_Knock_Knock_box_101 (saved by Fritzing 0.9.3b)
breadboards: 2

parts:
  J2 = Piezo Speaker
  R1 = Resistor [tolerance=±5% resistance=1M package=THT]
  VCC1 = Battery block 9V
  J3 = Piezo Speaker
  3v3_zener_diode = Zener Diode [part_number=1N4732A breakdown_voltage=3.6V package="300 mil [THT]"]
  Part1 = Arduino 101

nets:
  N1: J2.pin1, VCC1.-, J3.pin1, 3v3_zener_diode.anode, Part1.GND
  N2: J2.pin2, R1.Pin_0
  N3: R1.Pin_1, 3v3_zener_diode.cathode
  N4: VCC1.+, Part1.VIN
  N5: J3.pin2, Part1.D8

custom parts:
  Arduino 101: A learning and development board that delivers the performance and low-power consumption of the Intel® Curie™ Module with the simplicity of Arduino at an entry-level price. It keeps the same robust form factor and peripheral list of the UNO with the addition of onboard Bluetooth LE capabilities and a 6-axis accelerometer/gyro to help you easily expand your creativity into the connected world.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
