# Fritzing sketch Module_4_Camera_Robot_101 (saved by Fritzing 0.9.3b)
breadboards: 1

parts:
  J1 = Basic Servo
  J2 = Basic Servo
  VCC = 4 x AAA Battery Mount
  R1 = Rotary Potentiometer (Small) [maximum_resistance=10kΩ package=THT]
  R2 = Rotary Potentiometer (Small) [maximum_resistance=10kΩ package=THT]
  Part1 = Arduino 101

nets:
  GND: J1.gnd, J2.gnd, VCC.-, R1.leg2, R2.leg2, Part1.GND
  VCC: J1.vcc, J2.vcc, R1.leg1, R2.leg1, Part1.ioref
  N1: J1.pulse, Part1.D9_PWM
  N2: J2.pulse, Part1.D6_PWM
  N3: VCC.+, Part1.VIN
  N4: R1.wiper, Part1.A0
  N5: R2.wiper, Part1.A1

notes:
  8 x AAA

custom parts:
  Arduino 101: A learning and development board that delivers the performance and low-power consumption of the Intel® Curie™ Module with the simplicity of Arduino at an entry-level price. It keeps the same robust form factor and peripheral list of the UNO with the addition of onboard Bluetooth LE capabilities and a 6-axis accelerometer/gyro to help you easily expand your creativity into the connected world.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
