# Fritzing sketch Module_4_Light_Chaser_101 (saved by Fritzing 0.9.3b)
breadboards: 1

parts:
  R1 = Resistor [tolerance=±5% resistance=1k package=THT]
  R2 = Resistor [tolerance=±5% resistance=1k package=THT]
  J1 = Basic Servo
  J2 = Basic Servo
  VCC1 = 4 x AAA Battery Mount [part_number=4.8V]
  Q1 = LTR-301 [package=ltr-301]
  Q2 = LTR-301 [package=ltr-301]
  Part1 = Arduino 101
  VCC2 = Battery block 9V

nets (from the breadboard view):
  GND: R1.Pin_0, R2.Pin_0, J1.gnd, J2.gnd, VCC1.-, Part1.GND, VCC2.-
  N1: R1.Pin_1, Q2.E
  N2: R2.Pin_1, Q1.E
  VCC: J1.vcc, J2.vcc, VCC1.+
  N3: J1.pulse, Part1.D6_PWM
  N4: J2.pulse, Part1.D9_PWM
  N5: Q1.C, Q2.C, Part1.ioref
  N6: Part1.VIN, VCC2.+

notes:
  4 x AA

custom parts:
  Arduino 101: A learning and development board that delivers the performance and low-power consumption of the Intel® Curie™ Module with the simplicity of Arduino at an entry-level price. It keeps the same robust form factor and peripheral list of the UNO with the addition of onboard Bluetooth LE capabilities and a 6-axis accelerometer/gyro to help you easily expand your creativity into the connected world.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
