# Fritzing sketch Module_4_Magic_Box_101 (saved by Fritzing 0.9.3b)
breadboards: 1

parts:
  J1 = Basic Servo
  VCC1 = Battery block 9V
  J3 = Piezo Speaker
  3v3_zener_diode1 = Zener Diode [part_number=1N4732A breakdown_voltage=3.6V package="300 mil [THT]"]
  R2 = Resistor [tolerance=±5% resistance=1M package=THT]
  Part1 = Arduino 101

nets:
  GND: J1.gnd, VCC1.-, J3.pin1, 3v3_zener_diode1.anode, Part1.GND
  N1: J1.vcc, Part1.ioref
  N2: J1.pulse, Part1.D9_PWM
  N3: VCC1.+, Part1.VIN
  N4: J3.pin2, R2.Pin_0
  N5: 3v3_zener_diode1.cathode, R2.Pin_1, Part1.A0

custom parts:
  Arduino 101: A learning and development board that delivers the performance and low-power consumption of the Intel® Curie™ Module with the simplicity of Arduino at an entry-level price. It keeps the same robust form factor and peripheral list of the UNO with the addition of onboard Bluetooth LE capabilities and a 6-axis accelerometer/gyro to help you easily expand your creativity into the connected world.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
