# Fritzing sketch Module_05_Asteroid_attack_101 (saved by Fritzing 0.9.3b)
breadboards: 1

parts:
  S3 = Pushbutton [package="[THT]"]
  R3 = Resistor [tolerance=±5% resistance=10k package=THT]
  Part3 = Arduino 101

nets (from the schematic view):
  N1: S3.Pin_1, S3.Pin_2, R3.Pin_1, Part3.D5_PWM
  N2: S3.Pin_3, S3.Pin_4, Part3.ioref
  N3: R3.Pin_0, Part3.GND

custom parts:
  Arduino 101: A learning and development board that delivers the performance and low-power consumption of the Intel® Curie™ Module with the simplicity of Arduino at an entry-level price. It keeps the same robust form factor and peripheral list of the UNO with the addition of onboard Bluetooth LE capabilities and a 6-axis accelerometer/gyro to help you easily expand your creativity into the connected world.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
