# Fritzing sketch Module_05_Planet_finder_101 (saved by Fritzing 0.9.3b)
breadboards: 1

parts:
  Part5 = Arduino 101
  LED1 = LED - 5mm [color="Red (633nm)" package="5 mm [THT]"]
  J2 = Piezo Speaker
  R5 = Resistor [tolerance=±5% resistance=10k package=THT]
  VCC2 = Battery block 9V

nets:
  N1: Part5.D8, J2.pin1
  N2: Part5.D6_PWM, LED1.anode
  N3: Part5.GND, J2.pin2, R5.Pin_1, VCC2.-
  N4: Part5.VIN, VCC2.+
  N5: LED1.cathode, R5.Pin_0

custom parts:
  Arduino 101: A learning and development board that delivers the performance and low-power consumption of the Intel® Curie™ Module with the simplicity of Arduino at an entry-level price. It keeps the same robust form factor and peripheral list of the UNO with the addition of onboard Bluetooth LE capabilities and a 6-axis accelerometer/gyro to help you easily expand your creativity into the connected world.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
