# Fritzing sketch Module_05_Zazz_the_alien_101 (saved by Fritzing 0.9.3b)
breadboards: 1

parts:
  S4 = Pushbutton [package="[THT]"]
  R4 = Resistor [tolerance=±5% resistance=10k package=THT]
  R8 = Resistor [tolerance=±5% resistance=10k package=THT]
  Q2 = LTR-301 [package=ltr-301]
  Part4 = Arduino 101
  VCC3 = Battery block 9V

nets (from the schematic view):
  N1: S4.Pin_1, S4.Pin_2, R4.Pin_0, Part4.D10_PWM/SS
  N2: S4.Pin_3, S4.Pin_4, Q2.E, Part4.ioref
  N3: R4.Pin_1, R8.Pin_0, Part4.GND, VCC3.-
  N4: R8.Pin_1, Q2.C, Part4.A1
  N5: Part4.VIN, VCC3.+

custom parts:
  Arduino 101: A learning and development board that delivers the performance and low-power consumption of the Intel® Curie™ Module with the simplicity of Arduino at an entry-level price. It keeps the same robust form factor and peripheral list of the UNO with the addition of onboard Bluetooth LE capabilities and a 6-axis accelerometer/gyro to help you easily expand your creativity into the connected world.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
