# Fritzing sketch 2_Fencing (saved by Fritzing 0.9.0b)
breadboards: 1

parts:
  Parte1 = Arduino Uno (Rev3)
  LED1 = LED - 5mm [color="Yellow (595nm)" package="5 mm [THT]"]  # not connected
  LED2 = LED - 5mm [color="Red (633nm)" package="5 mm [THT]"]  # not connected
  LED3 = LED - 5mm [color="Green (555nm)" package="5 mm [THT]"]
  LED4 = LED - 5mm [color="Yellow (595nm)" package="5 mm [THT]"]  # not connected
  R1 = Resistor [tolerance=±5% resistance=220 package=THT]
  R2 = Resistor [tolerance=±5% resistance=220 package=THT]
  R4 = Resistor [tolerance=±5% resistance=220 package=THT]  # not connected
  S1 = Tilt Switch [package=THT]
  S2 = Tilt Switch [package=THT]
  R6 = Resistor [tolerance=±5% resistance=10k package=THT]
  R7 = Resistor [tolerance=±5% resistance=220 package=THT]
  R5 = Resistor [tolerance=±5% resistance=10k package=THT]

nets (from the breadboard view):
  N1: Parte1.D10_PWM/SS, S2.Pin_2, R5.Pin_0
  N2: Parte1.D3_PWM, R7.Pin_1
  N3: Parte1.D4, R2.Pin_1
  N4: Parte1.D6_PWM, R1.Pin_1
  N5: Parte1.5V, S1.Pin_2, S2.Pin_1
  N6: Parte1.GND, LED3.cathode, R6.Pin_0, R5.Pin_1
  N7: LED3.anode, R7.Pin_0
  N8: S1.Pin_1, R6.Pin_1
