# Fritzing sketch 5_Racing (saved by Fritzing 0.9.0b)
breadboards: 1

parts:
  Parte1 = Arduino Uno (Rev3)
  LED1 = LED - 5mm [color="Green (555nm)" package="5 mm [THT]"]
  LED2 = LED - 5mm [color="Green (555nm)" package="5 mm [THT]"]
  LED3 = LED - 5mm [color="Green (555nm)" package="5 mm [THT]"]
  R1 = Resistor [tolerance=±5% resistance=1M package=THT]
  R2 = Resistor [tolerance=±5% resistance=1M package=THT]
  R4 = Resistor [tolerance=±5% resistance=220 package=THT]
  R5 = Resistor [tolerance=±5% resistance=220 package=THT]
  R6 = Resistor [tolerance=±5% resistance=220 package=THT]
  R7 = Resistor [tolerance=±5% resistance=220 package=THT]
  R8 = Resistor [tolerance=±5% resistance=220 package=THT]
  LED4 = LED - 5mm [color="Green (555nm)" package="5 mm [THT]"]
  LED5 = LED - 5mm [color="Green (555nm)" package="5 mm [THT]"]

nets:
  N1: Parte1.D9_PWM, R8.Pin_0
  N2: Parte1.D10_PWM/SS, R7.Pin_0
  N3: Parte1.D11_PWM/MOSI, R6.Pin_0
  N4: Parte1.D12/MISO, R5.Pin_0
  N5: Parte1.D13/SCK, R4.Pin_0
  N6: Parte1.D2, R1.Pin_0, R2.Pin_0
  Aluminium foil: Parte1.D3_PWM, Parte1.D4, R1.Pin_1, R2.Pin_1
  N7: Parte1.GND, LED1.cathode, LED2.cathode, LED3.cathode, LED4.cathode, LED5.cathode
  N8: LED1.anode, R4.Pin_1
  N9: LED2.anode, R5.Pin_1
  N10: LED3.anode, R6.Pin_1
  N11: R7.Pin_1, LED4.anode
  N12: R8.Pin_1, LED5.anode

notes:
  Aluminium foil
