# Fritzing sketch 1_Cookie_Monster (saved by Fritzing 0.9.0b)
breadboards: 1

parts:
  Parte1 = Arduino Uno (Rev3)
  LED1 = LED - 5mm [color="White (6500K)" package="5 mm [THT]"]
  R1 = Resistor [tolerance=±5% resistance=220 package=THT]
  R2 = Resistor [tolerance=±5% resistance=1M package=THT]

nets:
  N1: Parte1.D9_PWM, R1.Pin_1
  N2: Parte1.GND, LED1.cathode
  N3: Parte1.D2, R2.Pin_0
  Aluminium foil: Parte1.D3_PWM, R2.Pin_1
  N4: LED1.anode, R1.Pin_0

notes:
  Aluminium foil
