# Fritzing sketch 2_Drawdio (saved by Fritzing 0.9.0b)
breadboards: 1

parts:
  Parte1 = Arduino Uno (Rev3)
  R1 = Resistor [tolerance=±5% resistance=1M package=THT]
  J1 = Piezo Speaker

nets:
  N1: Parte1.D8, J1.pin2
  N2: Parte1.GND, J1.pin1
  N3: Parte1.D2, R1.Pin_0
  Pencil.: Parte1.D3_PWM, R1.Pin_1

notes:
  Pencil
