# Fritzing sketch 4_POV (saved by Fritzing 0.9.0b)
breadboards: 1

parts:
  Parte1 = Arduino Uno (Rev3)
  LED1 = LED - 5mm [color="Green (555nm)" package="5 mm [THT]"]
  LED2 = LED - 5mm [color="Green (555nm)" package="5 mm [THT]"]
  LED3 = LED - 5mm [color="Green (555nm)" package="5 mm [THT]"]
  LED4 = LED - 5mm [color="Green (555nm)" package="5 mm [THT]"]
  LED5 = LED - 5mm [color="Green (555nm)" package="5 mm [THT]"]
  R1 = Resistor [tolerance=±5% resistance=220 package=THT]
  R2 = Resistor [tolerance=±5% resistance=220 package=THT]
  R3 = Resistor [tolerance=±5% resistance=220 package=THT]
  R4 = Resistor [tolerance=±5% resistance=220 package=THT]
  R5 = Resistor [tolerance=±5% resistance=220 package=THT]
  VCC1 = Battery block 9V

nets:
  N1: Parte1.GND, LED1.cathode, LED2.cathode, LED3.cathode, LED4.cathode, LED5.cathode, VCC1.-
  N2: Parte1.D2, R5.Pin_0
  N3: Parte1.D3_PWM, R4.Pin_0
  N4: Parte1.D4, R3.Pin_0
  N5: Parte1.D5_PWM, R2.Pin_0
  N6: Parte1.D6_PWM, R1.Pin_0
  N7: Parte1.VIN, VCC1.+
  N8: LED1.anode, R1.Pin_1
  N9: LED2.anode, R2.Pin_1
  N10: LED3.anode, R3.Pin_1
  N11: LED4.anode, R4.Pin_1
  N12: LED5.anode, R5.Pin_1
