# Fritzing sketch 5_Binary_LP (saved by Fritzing 0.9.0b)
breadboards: 1

parts:
  J1 = Piezo Speaker
  R1 = Resistor [tolerance=±5% resistance=220 package=THT]
  R2 = Resistor [tolerance=±5% resistance=220 package=THT]
  R3 = Resistor [tolerance=±5% resistance=220 package=THT]
  R4 = Resistor [tolerance=±5% resistance=47k package=THT]
  R5 = Resistor [tolerance=±5% resistance=47k package=THT]
  R6 = Resistor [tolerance=±5% resistance=47k package=THT]
  Parte1 = Arduino Uno (Rev3)
  S1 = CNY70 [package="[THT]"]
  S2 = CNY70 [package="[THT]"]
  S3 = CNY70 [package="[THT]"]

nets:
  N1: J1.pin1, Parte1.GND
  N2: J1.pin2, Parte1.D8
  N3: R1.Pin_0, R2.Pin_0, R3.Pin_0, R4.Pin_0, R5.Pin_0, R6.Pin_0, Parte1.A1, Parte1.A2, Parte1.A3, S1.Anode, S1.Catode, S1.Emiter, S1.Collector, S2.Anode, S2.Catode, S2.Emiter, S2.Collector, S3.Anode, S3.Catode, S3.Emiter, S3.Collector
  GND: R1.Pin_1, R2.Pin_1, R3.Pin_1, R4.Pin_1, R5.Pin_1, R6.Pin_1

custom parts:
  CNY70: IR compact sensor
