# Fritzing sketch Block_3_Knock_Knock_box (saved by Fritzing 0.9.0b)
breadboards: 1

parts:
  Parte1 = Arduino Uno (Rev3)
  J1 = Piezo Speaker
  J2 = Piezo Speaker
  R1 = Resistor [tolerance=±5% resistance=220 package=THT]
  VCC1 = Battery block 9V

nets:
  N1: Parte1.A0, J2.pin2, R1.Pin_1
  N2: Parte1.D8, J1.pin2
  N3: Parte1.GND, J1.pin1, J2.pin1, R1.Pin_0, VCC1.-
  N4: Parte1.VIN, VCC1.+
