# Fritzing sketch 2_Camera_Robot (saved by Fritzing 0.9.0b)
breadboards: 1

parts:
  Parte1 = Arduino Uno (Rev3)
  J1 = Basic Servo
  J2 = Basic Servo
  VCC = 4 x AAA Battery Mount
  R1 = Rotary Potentiometer (Small) [maximum_resistance=10kΩ package=THT]
  R2 = Rotary Potentiometer (Small) [maximum_resistance=10kΩ package=THT]

nets:
  N1: Parte1.A0, R1.wiper
  N2: Parte1.A1, R2.wiper
  N3: Parte1.D9_PWM, J2.pulse
  N4: Parte1.D10_PWM/SS, J1.pulse
  GND: Parte1.GND, J1.gnd, J2.gnd, VCC.-, R1.leg2, R2.leg2
  VCC: Parte1.VIN, J1.vcc, J2.vcc, VCC.+, R1.leg1, R2.leg1

notes:
  8 x AAA
