# Fritzing sketch 3_Tickle_Robot (saved by Fritzing 0.9.0b)
breadboards: 1

parts:
  Parte1 = Arduino Uno (Rev3)
  R1 = Resistor [tolerance=±5% resistance=1M package=THT]
  J1 = Basic Servo

nets:
  N1: Parte1.D9_PWM, J1.pulse
  GND: Parte1.GND, J1.gnd
  N2: Parte1.D2, R1.Pin_0
  Aluminium foil: Parte1.D3_PWM, R1.Pin_1
  5V: Parte1.5V, J1.vcc

notes:
  Aluminium foil
