# Fritzing sketch 4_Open_Box (saved by Fritzing 0.9.0b)
breadboards: 1

parts:
  Parte1 = Arduino Uno (Rev3)
  J1 = Basic Servo  # not connected
  J2 = Piezo Speaker
  R1 = Resistor [tolerance=±5% resistance=1M package=THT]

nets:
  N1: Parte1.A0, R1.Pin_0
  N2: Parte1.GND, J2.pin1, R1.Pin_1
