# Fritzing sketch 5_Light_Chaser (saved by Fritzing 0.9.0b)
breadboards: 1

parts:
  Parte1 = Arduino Uno (Rev3)
  R1 = Resistor [tolerance=±5% resistance=1k package=THT]
  R2 = Resistor [tolerance=±5% resistance=1k package=THT]
  R4 = Photocell (LDR) [package=THT]
  C1 = Electrolytic Capacitor [capacitance=100µF package="100 mil [THT, electrolytic]"]
  J1 = Basic Servo
  J2 = Basic Servo
  R3 = Photocell (LDR) [package=THT]
  VCC1 = 4 x AAA Battery Mount

nets:
  N1: Parte1.A0, R2.Pin_1, R4.pin_0
  N2: Parte1.A2, R1.Pin_1, R3.pin_0
  N3: Parte1.D9_PWM, J1.pulse
  N4: Parte1.D10_PWM/SS, J2.pulse
  GND: Parte1.GND, R1.Pin_0, R2.Pin_0, C1.-, J1.gnd, J2.gnd, VCC1.-
  N5: Parte1.VIN, VCC1.+
  VCC: R4.pin_1, J1.vcc, J2.vcc, R3.pin_1

notes:
  8 x AAA
