# Fritzing sketch Block_4_Robot (saved by Fritzing 0.9.0b)
breadboards: 1

parts:
  Parte1 = Arduino Uno (Rev3)
  J1 = Basic Servo
  J2 = Basic Servo
  VCC = 4 x AAA Battery Mount

nets:
  N1: Parte1.D9_PWM, J2.pulse
  N2: Parte1.D10_PWM/SS, J1.pulse
  GND: Parte1.GND, J1.gnd, J2.gnd, VCC.-
  VCC: Parte1.VIN, J1.vcc, J2.vcc, VCC.+

notes:
  8 batteries AA
