# Fritzing sketch Block_2_Digital_Die (saved by Fritzing 0.9.0b)
breadboards: 1

parts:
  LED1 = LED - 5mm [color="Red (633nm)" package="5 mm [THT]"]
  LED2 = LED - 5mm [color="Red (633nm)" package="5 mm [THT]"]
  LED3 = LED - 5mm [color="Red (633nm)" package="5 mm [THT]"]
  R3 = Resistor [tolerance=±5% resistance=220 package=THT]
  R1 = Resistor [tolerance=±5% resistance=220 package=THT]
  R2 = Resistor [tolerance=±5% resistance=220 package=THT]
  LED4 = LED - 5mm [color="Red (633nm)" package="5 mm [THT]"]
  LED5 = LED - 5mm [color="Red (633nm)" package="5 mm [THT]"]
  LED6 = LED - 5mm [color="Red (633nm)" package="5 mm [THT]"]
  R6 = Resistor [tolerance=±5% resistance=220 package=THT]
  R5 = Resistor [tolerance=±5% resistance=220 package=THT]
  R4 = Resistor [tolerance=±5% resistance=220 package=THT]
  LED7 = LED - 5mm [color="Red (633nm)" package="5 mm [THT]"]
  LED8 = LED - 5mm [color="Red (633nm)" package="5 mm [THT]"]
  LED9 = LED - 5mm [color="Red (633nm)" package="5 mm [THT]"]
  R9 = Resistor [tolerance=±5% resistance=220 package=THT]
  R8 = Resistor [tolerance=±5% resistance=220 package=THT]
  R7 = Resistor [tolerance=±5% resistance=220 package=THT]
  Parte1 = Arduino Uno (Rev3)
  S1 = Tilt Switch [package=THT]
  R10 = Resistor [tolerance=±5% resistance=10k package=THT]

nets:
  N1: LED1.cathode, LED2.cathode, LED3.cathode, LED4.cathode, LED5.cathode, LED6.cathode, LED7.cathode, LED8.cathode, LED9.cathode
  N2: LED1.anode, R1.Pin_1
  N3: LED2.anode, R2.Pin_1
  N4: LED3.anode, R3.Pin_0
  N5: R3.Pin_1, Parte1.D8
  N6: R1.Pin_0, Parte1.D12/MISO
  N7: R2.Pin_0, Parte1.D11_PWM/MOSI
  N8: LED4.anode, R4.Pin_1
  N9: LED5.anode, R5.Pin_1
  N10: LED6.anode, R6.Pin_0
  N11: R6.Pin_1, Parte1.D5_PWM
  N12: R5.Pin_0, Parte1.D6_PWM
  N13: R4.Pin_0, Parte1.D7
  N14: LED7.anode, R7.Pin_1
  N15: LED8.anode, R8.Pin_1
  N16: LED9.anode, R9.Pin_0
  N17: R9.Pin_1, Parte1.D2
  N18: R8.Pin_0, Parte1.D3_PWM
  N19: R7.Pin_0, Parte1.D4
  N20: Parte1.D9_PWM, S1.Pin_1, R10.Pin_1
  N21: Parte1.GND, R10.Pin_0
  5V: S1.Pin_2
