# Fritzing sketch Block_2_Pong (saved by Fritzing 0.9.0b)
breadboards: 1

parts:
  Parte1 = Arduino Uno (Rev3)
  LED1 = LED - 5mm [color="Green (555nm)" package="5 mm [THT]"]
  LED2 = LED - 5mm [color="Green (555nm)" package="5 mm [THT]"]
  LED3 = LED - 5mm [color="Green (555nm)" package="5 mm [THT]"]
  LED4 = LED - 5mm [color="Green (555nm)" package="5 mm [THT]"]
  LED5 = LED - 5mm [color="Green (555nm)" package="5 mm [THT]"]
  R1 = Resistor [tolerance=±5% resistance=220 package=THT]
  R2 = Resistor [tolerance=±5% resistance=220 package=THT]
  R3 = Resistor [tolerance=±5% resistance=220 package=THT]
  R4 = Resistor [tolerance=±5% resistance=220 package=THT]
  R5 = Resistor [tolerance=±5% resistance=220 package=THT]
  S1 = Pushbutton [package="[THT]"]
  S2 = Pushbutton [package="[THT]"]
  R6 = Resistor [tolerance=±5% resistance=220 package=THT]
  R7 = Resistor [tolerance=±5% resistance=220 package=THT]

nets:
  N1: Parte1.D9_PWM, S1.Pin_1, S1.Pin_2, R7.Pin_0
  N2: Parte1.D10_PWM/SS, S2.Pin_1, S2.Pin_2, R6.Pin_0
  N3: Parte1.GND, LED1.cathode, LED2.cathode, LED3.cathode, LED4.cathode, LED5.cathode, R6.Pin_1, R7.Pin_1
  N4: Parte1.D2, R1.Pin_1
  N5: Parte1.D3_PWM, R3.Pin_1
  N6: Parte1.D4, R4.Pin_1
  N7: Parte1.D5_PWM, R5.Pin_1
  N8: Parte1.D6_PWM, R2.Pin_1
  N9: Parte1.5V, S1.Pin_3, S1.Pin_4, S2.Pin_3, S2.Pin_4
  N10: LED1.anode, R5.Pin_0
  N11: LED2.anode, R2.Pin_0
  N12: LED3.anode, R4.Pin_0
  N13: LED4.anode, R3.Pin_0
  N14: LED5.anode, R1.Pin_0
