# Fritzing sketch Block_2_React_Schematic (saved by Fritzing 0.9.0b)
breadboards: 1

parts:
  Parte1 = Arduino Uno (Rev3)
  LED1 = LED - 5mm [color="Red (633nm)" package="5 mm [THT]"]
  LED2 = LED - 5mm [color="Red (633nm)" package="5 mm [THT]"]
  LED3 = LED - 5mm [color="Red (633nm)" package="5 mm [THT]"]
  J1 = Piezo Speaker
  R1 = Resistor [tolerance=±5% resistance=1M package=THT]
  R2 = Resistor [tolerance=±5% resistance=1M package=THT]
  R3 = Resistor [tolerance=±5% resistance=1M package=THT]
  R4 = Resistor [tolerance=±5% resistance=220 package=THT]
  R5 = Resistor [tolerance=±5% resistance=220 package=THT]
  R6 = Resistor [tolerance=±5% resistance=220 package=THT]

nets:
  N1: Parte1.D8, J1.pin2
  N2: Parte1.D9_PWM, R6.Pin_0
  N3: Parte1.D10_PWM/SS, R5.Pin_0
  N4: Parte1.D11_PWM/MOSI, R4.Pin_0
  N5: Parte1.D2, R1.Pin_0, R2.Pin_0, R3.Pin_0
  Aluminium foil: Parte1.D3_PWM, Parte1.D4, Parte1.D5_PWM, R1.Pin_1, R2.Pin_1, R3.Pin_1
  N6: Parte1.GND, LED1.cathode, LED2.cathode, LED3.cathode, J1.pin1
  N7: LED1.anode, R4.Pin_1
  N8: LED2.anode, R5.Pin_1
  N9: LED3.anode, R6.Pin_1

notes:
  Aluminium foil
