# Fritzing sketch Block_2_Simon_Says (saved by Fritzing 0.9.0b)
breadboards: 1

parts:
  Parte1 = Arduino Uno (Rev3)
  LED1 = LED - 5mm [color="Yellow (585nm)" package="5 mm [THT]"]
  LED2 = LED - 5mm [color="Yellow (585nm)" package="5 mm [THT]"]
  LED3 = LED - 5mm [color="Yellow (585nm)" package="5 mm [THT]"]
  LED4 = LED - 5mm [color="Yellow (585nm)" package="5 mm [THT]"]
  LED5 = LED - 5mm [color="Yellow (585nm)" package="5 mm [THT]"]
  R1 = Resistor [tolerance=±5% resistance=220 package=THT]
  R2 = Resistor [tolerance=±5% resistance=220 package=THT]
  R3 = Resistor [tolerance=±5% resistance=220 package=THT]
  R4 = Resistor [tolerance=±5% resistance=220 package=THT]
  R5 = Resistor [tolerance=±5% resistance=220 package=THT]
  J1 = Piezo Speaker
  R6 = Rotary Potentiometer (Small) [maximum_resistance=100kΩ package=THT]
  S1 = Pushbutton [package="[THT]"]
  R7 = Resistor [tolerance=±5% resistance=10k package=THT]

nets:
  N1: Parte1.A0, R6.wiper
  N2: Parte1.D8, J1.pin2
  N3: Parte1.D9_PWM, S1.Pin_1, S1.Pin_2, R7.Pin_0
  N4: Parte1.D2, R5.Pin_0
  N5: Parte1.D3_PWM, R4.Pin_0
  N6: Parte1.D4, R3.Pin_0
  N7: Parte1.D5_PWM, R2.Pin_0
  N8: Parte1.D6_PWM, R1.Pin_0
  N9: Parte1.5V, R6.leg2
  N10: Parte1.GND, LED1.cathode, LED2.cathode, LED3.cathode, LED4.cathode, LED5.cathode, J1.pin1, R6.leg1, S1.Pin_3, S1.Pin_4, R7.Pin_1
  N11: LED1.anode, R1.Pin_1
  N12: LED2.anode, R2.Pin_1
  N13: LED3.anode, R3.Pin_1
  N14: LED4.anode, R4.Pin_1
  N15: LED5.anode, R5.Pin_1
