# Fritzing sketch Block_4_Line_Follower (saved by Fritzing 0.9.0b)
breadboards: 1

parts:
  S3 = CNY70 [package="[THT]"]
  R1 = Resistor [tolerance=±5% resistance=220 package=THT]
  R2 = Resistor [tolerance=±5% resistance=220 package=THT]
  R3 = Resistor [tolerance=±5% resistance=220 package=THT]
  R4 = Resistor [tolerance=±5% resistance=47k package=THT]
  R5 = Resistor [tolerance=±5% resistance=47k package=THT]
  R6 = Resistor [tolerance=±5% resistance=47k package=THT]
  Parte1 = Arduino Uno (Rev3)
  VCC1 = Battery block 9V
  VCC2 = 4 x AAA Battery Mount
  J1 = Basic Servo
  J2 = Basic Servo
  S1 = CNY70 [package="[THT]"]
  S2 = CNY70 [package="[THT]"]

nets:
  N1: S3.Anode, R3.Pin_0
  GND: S3.Catode, S3.Emiter, Parte1.GND, VCC1.-, VCC2.-, J1.gnd, J2.gnd, S1.Catode, S1.Emiter, S2.Catode, S2.Emiter
  N2: S3.Collector, R4.Pin_1, Parte1.A1
  N3: R1.Pin_0, S1.Anode
  N4: R1.Pin_1, R2.Pin_1, R3.Pin_1, R4.Pin_0, R5.Pin_0, R6.Pin_0, Parte1.5V
  N5: R2.Pin_0, S2.Anode
  N6: R5.Pin_1, Parte1.A2, S2.Collector
  N7: R6.Pin_1, Parte1.A3, S1.Collector
  N8: Parte1.D9_PWM, J1.pulse
  N9: Parte1.D10_PWM/SS, J2.pulse
  N10: Parte1.VIN, VCC1.+
  VCC: VCC2.+, J1.vcc, J2.vcc

custom parts:
  CNY70: IR compact sensor
