# Fritzing sketch Block_4_Open_Box (saved by Fritzing 0.9.0b)
breadboards: 1

parts:
  Parte1 = Arduino Uno (Rev3)
  J1 = Basic Servo
  J2 = Piezo Speaker
  R1 = Resistor [tolerance=±5% resistance=1M package=THT]
  VCC1 = Battery block 9V

nets:
  N1: Parte1.A0, J2.pin2, R1.Pin_0
  N2: Parte1.D9_PWM, J1.pulse
  GND: Parte1.GND, J1.gnd, J2.pin1, R1.Pin_1, VCC1.-
  5V: Parte1.5V, J1.vcc
  N3: Parte1.VIN, VCC1.+
