# Fritzing sketch Block_2_Digital_Die_UNO (saved by Fritzing 0.9.3b)
breadboards: 1

parts:
  LED1 = LED - 5mm [color="Red (633nm)" package="5 mm [THT]"]
  LED2 = LED - 5mm [color="Red (633nm)" package="5 mm [THT]"]
  LED3 = LED - 5mm [color="Red (633nm)" package="5 mm [THT]"]
  R3 = Resistor [tolerance=±5% resistance=220 package=THT]
  R1 = Resistor [tolerance=±5% resistance=220 package=THT]
  R2 = Resistor [tolerance=±5% resistance=220 package=THT]
  LED4 = LED - 5mm [color="Red (633nm)" package="5 mm [THT]"]
  LED5 = LED - 5mm [color="Red (633nm)" package="5 mm [THT]"]
  LED6 = LED - 5mm [color="Red (633nm)" package="5 mm [THT]"]
  R6 = Resistor [tolerance=±5% resistance=220 package=THT]
  R5 = Resistor [tolerance=±5% resistance=220 package=THT]
  R4 = Resistor [tolerance=±5% resistance=220 package=THT]
  LED7 = LED - 5mm [color="Red (633nm)" package="5 mm [THT]"]
  LED8 = LED - 5mm [color="Red (633nm)" package="5 mm [THT]"]
  LED9 = LED - 5mm [color="Red (633nm)" package="5 mm [THT]"]
  R9 = Resistor [tolerance=±5% resistance=220 package=THT]
  R8 = Resistor [tolerance=±5% resistance=220 package=THT]
  R7 = Resistor [tolerance=±5% resistance=220 package=THT]
  S1 = Tilt Switch [package=THT]
  R10 = Resistor [tolerance=±5% resistance=10k package=THT]
  Part1 = Genuino Uno (Rev3)

nets:
  N1: LED1.cathode, LED2.cathode, LED3.cathode, LED4.cathode, LED5.cathode, LED6.cathode, LED7.cathode, LED8.cathode, LED9.cathode, R10.Pin_0, Part1.GND
  N2: LED1.anode, R1.Pin_1
  N3: LED2.anode, R2.Pin_1
  N4: LED3.anode, R3.Pin_0
  N5: R3.Pin_1, Part1.D8
  N6: R1.Pin_0, Part1.D12/MISO
  N7: R2.Pin_0, Part1.D11_PWM/MOSI
  N8: LED4.anode, R4.Pin_1
  N9: LED5.anode, R5.Pin_1
  N10: LED6.anode, R6.Pin_0
  N11: R6.Pin_1, Part1.D5_PWM
  N12: R5.Pin_0, Part1.D6_PWM
  N13: R4.Pin_0, Part1.D7
  N14: LED7.anode, R7.Pin_1
  N15: LED8.anode, R8.Pin_1
  N16: LED9.anode, R9.Pin_0
  N17: R9.Pin_1, Part1.D2
  N18: R8.Pin_0, Part1.D3_PWM
  N19: R7.Pin_0, Part1.D4
  N20: S1.Pin_1, R10.Pin_1, Part1.D9_PWM
  N21: S1.Pin_2, Part1.ioref

custom parts:
  Genuino Uno (Rev3): The Arduino Uno is a microcontroller board based on the ATmega328 (datasheet). It has 14 digital input/output pins (of which 6 can be used as PWM outputs), 6 analog inputs, a 16 MHz ceramic resonator, a USB connection, a power jack, an ICSP header, and a reset button. It contains everything needed to support the microcontroller; simply connect it to a computer with a USB cable or power it with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
