# Fritzing sketch Block_2_Fencing_UNO (saved by Fritzing 0.9.3b)
breadboards: 1

parts:
  LED1 = LED - 5mm [color="Yellow (595nm)" package="5 mm [THT]"]
  LED2 = LED - 5mm [color="Red (633nm)" package="5 mm [THT]"]
  LED3 = LED - 5mm [color="Green (555nm)" package="5 mm [THT]"]
  LED4 = LED - 5mm [color="Yellow (595nm)" package="5 mm [THT]"]
  R4 = Resistor [tolerance=±5% resistance=220 package=THT]
  R3 = Resistor [tolerance=±5% resistance=220 package=THT]
  S1 = Tilt Switch [package=THT]
  S2 = Tilt Switch [package=THT]
  R6 = Resistor [tolerance=±5% resistance=10k package=THT]
  R5 = Resistor [tolerance=±5% resistance=10k package=THT]
  Part1 = Genuino Uno (Rev3)
  R2 = Resistor [tolerance=±5% resistance=220 package=THT]
  R1 = Resistor [tolerance=±5% resistance=220 package=THT]

nets (from the breadboard view):
  N1: LED1.cathode, LED2.cathode, LED3.cathode, LED4.cathode, R6.Pin_0, R5.Pin_1, Part1.GND
  N2: LED1.anode, R4.Pin_0
  N3: LED2.anode, R3.Pin_0
  N4: LED3.anode, R2.Pin_0
  N5: LED4.anode, R1.Pin_0
  N6: R4.Pin_1, Part1.D5_PWM
  N7: R3.Pin_1, Part1.D4
  N8: S1.Pin_1, R6.Pin_1
  N9: S1.Pin_2, S2.Pin_1, Part1.ioref
  N10: S2.Pin_2, R5.Pin_0, Part1.D9_PWM
  N11: Part1.D2, R1.Pin_1
  N12: Part1.D3_PWM, R2.Pin_1

custom parts:
  Genuino Uno (Rev3): The Arduino Uno is a microcontroller board based on the ATmega328 (datasheet). It has 14 digital input/output pins (of which 6 can be used as PWM outputs), 6 analog inputs, a 16 MHz ceramic resonator, a USB connection, a power jack, an ICSP header, and a reset button. It contains everything needed to support the microcontroller; simply connect it to a computer with a USB cable or power it with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
