# Fritzing sketch Block_2_Pong_UNO (saved by Fritzing 0.9.3b)
breadboards: 1

parts:
  LED1 = LED - 5mm [color="Green (555nm)" package="5 mm [THT]"]
  LED2 = LED - 5mm [color="Green (555nm)" package="5 mm [THT]"]
  LED3 = LED - 5mm [color="Green (555nm)" package="5 mm [THT]"]
  LED4 = LED - 5mm [color="Green (555nm)" package="5 mm [THT]"]
  LED5 = LED - 5mm [color="Green (555nm)" package="5 mm [THT]"]
  R1 = Resistor [tolerance=±5% resistance=220 package=THT]
  R2 = Resistor [tolerance=±5% resistance=220 package=THT]
  R3 = Resistor [tolerance=±5% resistance=220 package=THT]
  R4 = Resistor [tolerance=±5% resistance=220 package=THT]
  S1 = Pushbutton [package="[THT]"]
  S2 = Pushbutton [package="[THT]"]
  Part1 = Genuino Uno (Rev3)
  R8 = Resistor [tolerance=±5% resistance=10k package=THT]
  R9 = Resistor [tolerance=±5% resistance=10k package=THT]
  R10 = Resistor [tolerance=±5% resistance=220 package=THT]

nets (from the schematic view):
  N1: LED1.cathode, LED2.cathode, LED3.cathode, LED4.cathode, LED5.cathode, Part1.GND, R8.Pin_0, R9.Pin_0
  N2: LED1.anode, R1.Pin_1
  N3: LED2.anode, R2.Pin_1
  N4: LED3.anode, R10.Pin_1
  N5: LED4.anode, R3.Pin_1
  N6: LED5.anode, R4.Pin_1
  N7: R1.Pin_0, Part1.D2
  N8: R2.Pin_0, Part1.D5_PWM
  N9: R3.Pin_0, Part1.D3_PWM
  N10: R4.Pin_0, Part1.D7
  N11: S1.Pin_1, S1.Pin_2, S2.Pin_1, S2.Pin_2, Part1.ioref
  N12: S1.Pin_3, S1.Pin_4, Part1.D6_PWM, R8.Pin_1
  N13: S2.Pin_3, S2.Pin_4, Part1.D9_PWM, R9.Pin_1
  N14: Part1.D4, R10.Pin_0

custom parts:
  Genuino Uno (Rev3): The Arduino Uno is a microcontroller board based on the ATmega328 (datasheet). It has 14 digital input/output pins (of which 6 can be used as PWM outputs), 6 analog inputs, a 16 MHz ceramic resonator, a USB connection, a power jack, an ICSP header, and a reset button. It contains everything needed to support the microcontroller; simply connect it to a computer with a USB cable or power it with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
