# Fritzing sketch Block_2_Racing_UNO (saved by Fritzing 0.9.3b)
breadboards: 1

parts:
  LED1 = LED - 5mm [color="Green (555nm)" package="5 mm [THT]"]
  LED2 = LED - 5mm [color="Green (555nm)" package="5 mm [THT]"]
  LED3 = LED - 5mm [color="Green (555nm)" package="5 mm [THT]"]
  R1 = Resistor [tolerance=±5% resistance=1M package=THT]
  R2 = Resistor [tolerance=±5% resistance=1M package=THT]
  R4 = Resistor [tolerance=±5% resistance=220 package=THT]
  R5 = Resistor [tolerance=±5% resistance=220 package=THT]
  R6 = Resistor [tolerance=±5% resistance=220 package=THT]
  R7 = Resistor [tolerance=±5% resistance=220 package=THT]
  R8 = Resistor [tolerance=±5% resistance=220 package=THT]
  LED4 = LED - 5mm [color="Green (555nm)" package="5 mm [THT]"]
  LED5 = LED - 5mm [color="Green (555nm)" package="5 mm [THT]"]
  Part1 = Genuino Uno (Rev3)

nets:
  N1: LED1.cathode, LED2.cathode, LED3.cathode, LED4.cathode, LED5.cathode, Part1.GND
  N2: LED1.anode, R4.Pin_1
  N3: LED2.anode, R5.Pin_1
  N4: LED3.anode, R6.Pin_1
  N5: R1.Pin_0, R2.Pin_0, Part1.D2
  Aluminium foil: R1.Pin_1, Part1.D4
  N6: R2.Pin_1, Part1.D3_PWM
  N7: R4.Pin_0, Part1.D13/SCK
  N8: R5.Pin_0, Part1.D11_PWM/MOSI
  N9: R6.Pin_0, Part1.D10_PWM/SS
  N10: R7.Pin_0, Part1.D9_PWM
  N11: R7.Pin_1, LED4.anode
  N12: R8.Pin_0, Part1.D8
  N13: R8.Pin_1, LED5.anode

notes:
  Aluminium foil

custom parts:
  Genuino Uno (Rev3): The Arduino Uno is a microcontroller board based on the ATmega328 (datasheet). It has 14 digital input/output pins (of which 6 can be used as PWM outputs), 6 analog inputs, a 16 MHz ceramic resonator, a USB connection, a power jack, an ICSP header, and a reset button. It contains everything needed to support the microcontroller; simply connect it to a computer with a USB cable or power it with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
