# Fritzing sketch Block_3_Binary_LP_Schematic_UNO (saved by Fritzing 0.9.3b)
breadboards: 1

parts:
  J1 = Piezo Speaker
  R1 = Resistor [tolerance=±5% resistance=220 package=THT]
  R2 = Resistor [tolerance=±5% resistance=220 package=THT]
  R3 = Resistor [tolerance=±5% resistance=220 package=THT]
  R4 = Resistor [tolerance=±5% resistance=47k package=THT]
  R5 = Resistor [tolerance=±5% resistance=47k package=THT]
  R6 = Resistor [tolerance=±5% resistance=47k package=THT]
  S1 = CNY70 [package="[THT]"]
  S2 = CNY70 [package="[THT]"]
  S3 = CNY70 [package="[THT]"]
  Part1 = Genuino Uno (Rev3)

nets:
  N1: J1.pin1, R4.Pin_0, R5.Pin_0, R6.Pin_0, S1.Catode, S2.Catode, S3.Catode, Part1.GND
  N2: J1.pin2, Part1.D8
  N3: R1.Pin_0, S1.Anode
  N4: R1.Pin_1, R2.Pin_1, R3.Pin_1, S3.Collector, Part1.ioref
  N5: R2.Pin_0, S2.Anode
  N6: R3.Pin_0, S3.Anode
  N7: R4.Pin_1, S1.Emiter
  N8: R5.Pin_1, S2.Emiter
  N9: R6.Pin_1, S3.Emiter
  N10: S1.Collector, S2.Collector

custom parts:
  CNY70: IR compact sensor
  Genuino Uno (Rev3): The Arduino Uno is a microcontroller board based on the ATmega328 (datasheet). It has 14 digital input/output pins (of which 6 can be used as PWM outputs), 6 analog inputs, a 16 MHz ceramic resonator, a USB connection, a power jack, an ICSP header, and a reset button. It contains everything needed to support the microcontroller; simply connect it to a computer with a USB cable or power it with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
