# Fritzing sketch Block_3_Cookie_Monster_UNO (saved by Fritzing 0.9.3b)
breadboards: 1

parts:
  LED1 = LED - 5mm [color="White (6500K)" package="5 mm [THT]"]
  R1 = Resistor [tolerance=±5% resistance=220 package=THT]
  R2 = Resistor [tolerance=±5% resistance=1M package=THT]
  Part1 = Genuino Uno (Rev3)

nets:
  N1: LED1.cathode, Part1.GND
  N2: LED1.anode, R1.Pin_0
  N3: R1.Pin_1, Part1.D9_PWM
  N4: R2.Pin_0, Part1.D2
  Aluminium foil: R2.Pin_1, Part1.D3_PWM

notes:
  Aluminium foil

custom parts:
  Genuino Uno (Rev3): The Arduino Uno is a microcontroller board based on the ATmega328 (datasheet). It has 14 digital input/output pins (of which 6 can be used as PWM outputs), 6 analog inputs, a 16 MHz ceramic resonator, a USB connection, a power jack, an ICSP header, and a reset button. It contains everything needed to support the microcontroller; simply connect it to a computer with a USB cable or power it with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
