# Fritzing sketch Block_3_Knock_Knock_box_UNO (saved by Fritzing 0.9.3b)
breadboards: 2

parts:
  J2 = Piezo Speaker
  R1 = Resistor [tolerance=±5% resistance=1M package=THT]
  VCC1 = Battery block 9V
  J3 = Piezo Speaker
  Part1 = Genuino Uno (Rev3)
  3v3_zener_diode = Zener Diode [part_number=1N4732A breakdown_voltage=3.6V package="300 mil [THT]"]

nets:
  N1: J2.pin1, VCC1.-, J3.pin1, Part1.GND, 3v3_zener_diode.anode
  N2: J2.pin2, R1.Pin_0
  N3: R1.Pin_1, 3v3_zener_diode.cathode
  N4: VCC1.+, Part1.VIN
  N5: J3.pin2, Part1.D8

custom parts:
  Genuino Uno (Rev3): The Arduino Uno is a microcontroller board based on the ATmega328 (datasheet). It has 14 digital input/output pins (of which 6 can be used as PWM outputs), 6 analog inputs, a 16 MHz ceramic resonator, a USB connection, a power jack, an ICSP header, and a reset button. It contains everything needed to support the microcontroller; simply connect it to a computer with a USB cable or power it with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
