# Fritzing sketch Block_4_Camera_Robot_UNO (saved by Fritzing 0.9.3b)
breadboards: 1

parts:
  J1 = Basic Servo
  J2 = Basic Servo
  VCC = 4 x AAA Battery Mount
  R1 = Rotary Potentiometer (Small) [maximum_resistance=10kΩ package=THT]
  R2 = Rotary Potentiometer (Small) [maximum_resistance=10kΩ package=THT]
  Part1 = Genuino Uno (Rev3)

nets:
  GND: J1.gnd, J2.gnd, VCC.-, R1.leg2, R2.leg2, Part1.GND
  VCC: J1.vcc, J2.vcc, R1.leg1, R2.leg1, Part1.ioref
  N1: J1.pulse, Part1.D9_PWM
  N2: J2.pulse, Part1.D6_PWM
  N3: VCC.+, Part1.VIN
  N4: R1.wiper, Part1.A0
  N5: R2.wiper, Part1.A1

notes:
  8 x AAA

custom parts:
  Genuino Uno (Rev3): The Arduino Uno is a microcontroller board based on the ATmega328 (datasheet). It has 14 digital input/output pins (of which 6 can be used as PWM outputs), 6 analog inputs, a 16 MHz ceramic resonator, a USB connection, a power jack, an ICSP header, and a reset button. It contains everything needed to support the microcontroller; simply connect it to a computer with a USB cable or power it with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
