# Fritzing sketch Block_4_Crawling_Robot_UNO (saved by Fritzing 0.9.3b)
breadboards: 1

parts:
  J1 = Basic Servo
  J2 = Basic Servo
  VCC = 4 x AAA Battery Mount
  Part1 = Genuino Uno (Rev3)

nets:
  GND: J1.gnd, J2.gnd, VCC.-, Part1.GND
  VCC: J1.vcc, J2.vcc, Part1.ioref
  N1: J1.pulse, Part1.D9_PWM
  N2: J2.pulse, Part1.D6_PWM
  N3: VCC.+, Part1.VIN

notes:
  8 batteries AA

custom parts:
  Genuino Uno (Rev3): The Arduino Uno is a microcontroller board based on the ATmega328 (datasheet). It has 14 digital input/output pins (of which 6 can be used as PWM outputs), 6 analog inputs, a 16 MHz ceramic resonator, a USB connection, a power jack, an ICSP header, and a reset button. It contains everything needed to support the microcontroller; simply connect it to a computer with a USB cable or power it with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
