# Fritzing sketch Block_4_Light_Chaser_UNO (saved by Fritzing 0.9.3b)
breadboards: 1

parts:
  R1 = Resistor [tolerance=±5% resistance=1k package=THT]
  R2 = Resistor [tolerance=±5% resistance=1k package=THT]
  C1 = Electrolytic Capacitor [capacitance=100µF package="100 mil [THT, electrolytic]"]
  J1 = Basic Servo
  J2 = Basic Servo
  VCC1 = 4 x AAA Battery Mount
  Q1 = LTR-301 [package=ltr-301]
  Q2 = LTR-301 [package=ltr-301]
  Part1 = Genuino Uno (Rev3)

nets (from the schematic view):
  GND: R1.Pin_0, R2.Pin_0, C1.-, J1.gnd, J2.gnd, VCC1.-, Part1.GND
  N1: R1.Pin_1, Q2.C, Part1.A2
  N2: R2.Pin_1, Q1.C, Part1.A0
  VCC: C1.+, J1.vcc, J2.vcc, Q1.E, Q2.E, Part1.ioref
  N3: J1.pulse, Part1.D6_PWM
  N4: J2.pulse, Part1.D9_PWM
  N5: VCC1.+, Part1.VIN

notes:
  8 x AAA

custom parts:
  Genuino Uno (Rev3): The Arduino Uno is a microcontroller board based on the ATmega328 (datasheet). It has 14 digital input/output pins (of which 6 can be used as PWM outputs), 6 analog inputs, a 16 MHz ceramic resonator, a USB connection, a power jack, an ICSP header, and a reset button. It contains everything needed to support the microcontroller; simply connect it to a computer with a USB cable or power it with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
