# Fritzing sketch Block_4_Line_Follower_UNO (saved by Fritzing 0.9.3b)
breadboards: 1

parts:
  R1 = Resistor [tolerance=±5% resistance=220 package=THT]
  R2 = Resistor [tolerance=±5% resistance=220 package=THT]
  R3 = Resistor [tolerance=±5% resistance=220 package=THT]
  R4 = Resistor [tolerance=±5% resistance=47k package=THT]
  R5 = Resistor [tolerance=±5% resistance=47k package=THT]
  R6 = Resistor [tolerance=±5% resistance=47k package=THT]
  VCC1 = Battery block 9V
  VCC2 = 4 x AAA Battery Mount
  J1 = Basic Servo
  J2 = Basic Servo
  S1 = CNY70 [package="[THT]"]
  S2 = CNY70 [package="[THT]"]
  Part1 = Genuino Uno (Rev3)
  S3 = CNY70 [package="[THT]"]

nets (from the schematic view):
  N1: R1.Pin_0, R2.Pin_0, R3.Pin_1, S1.Collector, S2.Collector, Part1.ioref, S3.Collector
  N2: R1.Pin_1, S1.Anode
  N3: R2.Pin_1, S2.Anode
  N4: R3.Pin_0, S3.Anode
  N5: R4.Pin_0, R5.Pin_0, R6.Pin_0, VCC1.-, S1.Catode, S2.Catode, Part1.GND, S3.Catode
  N6: R4.Pin_1, Part1.A1, S3.Emiter
  N7: R5.Pin_1, S2.Emiter, Part1.A2
  N8: R6.Pin_1, S1.Emiter, Part1.A3
  N9: VCC1.+, Part1.VIN
  GND: VCC2.-, J1.gnd, J2.gnd
  VCC: VCC2.+, J1.vcc, J2.vcc
  N10: J1.pulse, Part1.D6_PWM
  N11: J2.pulse, Part1.D9_PWM

custom parts:
  CNY70: IR compact sensor
  Genuino Uno (Rev3): The Arduino Uno is a microcontroller board based on the ATmega328 (datasheet). It has 14 digital input/output pins (of which 6 can be used as PWM outputs), 6 analog inputs, a 16 MHz ceramic resonator, a USB connection, a power jack, an ICSP header, and a reset button. It contains everything needed to support the microcontroller; simply connect it to a computer with a USB cable or power it with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
