# Fritzing sketch Block_4_Magic_Box_UNO (saved by Fritzing 0.9.3b)
breadboards: 1

parts:
  J1 = Basic Servo
  VCC1 = Battery block 9V
  J3 = Piezo Speaker
  3v3_zener_diode1 = Zener Diode [part_number=1N4732A breakdown_voltage=3.6V package="300 mil [THT]"]
  R2 = Resistor [tolerance=±5% resistance=1M package=THT]
  Part1 = Genuino Uno (Rev3)

nets:
  GND: J1.gnd, VCC1.-, J3.pin1, 3v3_zener_diode1.anode, Part1.GND
  N1: J1.vcc, Part1.ioref
  N2: J1.pulse, Part1.D9_PWM
  N3: VCC1.+, Part1.VIN
  N4: J3.pin2, R2.Pin_0
  N5: 3v3_zener_diode1.cathode, R2.Pin_1

custom parts:
  Genuino Uno (Rev3): The Arduino Uno is a microcontroller board based on the ATmega328 (datasheet). It has 14 digital input/output pins (of which 6 can be used as PWM outputs), 6 analog inputs, a 16 MHz ceramic resonator, a USB connection, a power jack, an ICSP header, and a reset button. It contains everything needed to support the microcontroller; simply connect it to a computer with a USB cable or power it with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
