# Fritzing sketch Block_4_Tickle_Robot_UNO (saved by Fritzing 0.9.3b)
breadboards: 1

parts:
  R1 = Resistor [tolerance=±5% resistance=1M package=THT]
  J1 = Basic Servo
  Part1 = Genuino Uno (Rev3)

nets:
  N1: R1.Pin_0, Part1.D2
  Aluminium foil: R1.Pin_1, Part1.D3_PWM
  GND: J1.gnd, Part1.GND
  N2: J1.vcc, Part1.ioref
  N3: J1.pulse, Part1.D9_PWM

notes:
  Aluminium foil

custom parts:
  Genuino Uno (Rev3): The Arduino Uno is a microcontroller board based on the ATmega328 (datasheet). It has 14 digital input/output pins (of which 6 can be used as PWM outputs), 6 analog inputs, a 16 MHz ceramic resonator, a USB connection, a power jack, an ICSP header, and a reset button. It contains everything needed to support the microcontroller; simply connect it to a computer with a USB cable or power it with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
